# Fritzing sketch test-taster-01 (saved by Fritzing 1.0.5)
breadboards: 1

parts:
  VCC1 = Battery [internal_resistance=0.1Ω]
  R1 = Resistor [tolerance=±5% power=0.25W resistance=220 package=THT]
  LED1 = LED - 5mm [color="Red (633nm)" current=0.030A package="5 mm [THT]"]
  R2 = Resistor [tolerance=±5% power=0.25W resistance=220 package=THT]
  S1 = Pushbutton [package="[THT]"]
  Bauteil1 = Arduino Mega ADK (Rev3)  # not connected

nets:
  N1: VCC1.-, R1.Pin_0, LED1.cathode
  N2: VCC1.+, S1.Pin_3, S1.Pin_4
  N3: R1.Pin_1, R2.Pin_1, S1.Pin_1, S1.Pin_2
  N4: LED1.anode, R2.Pin_0

// code stored in the sketch: test-taster-01.ino
// Test
