# Fritzing sketch wb25-alpha01 (saved by Fritzing 1.0.5)
breadboards: 1

parts:
  Bauteil1 = Arduino Mega ADK (Rev3)
  M1 = BTS7960
  S1 = Pushbutton [package="[THT]"]
  VCC1 = Battery block 9V [internal_resistance=0.1Ω]
  Gleis = DC Motor [voltage_(max)=6V voltage_(min)=3V]

nets:
  N1: Bauteil1.A0, M1.pin5
  N2: Bauteil1.A1, M1.pin6
  N3: Bauteil1.D8_PWM, M1.pin4
  N4: Bauteil1.5V, M1.pin7
  N5: Bauteil1.GND, M1.pin8
  N6: Bauteil1.D5_PWM, M1.pin1
  N7: Bauteil1.D6_PWM, M1.pin2
  N8: Bauteil1.D7_PWM, M1.pin3
  N9: M1.pin9, Gleis.pin_2
  N10: M1.pin10, Gleis.pin_1
  N11: M1.pin11, VCC1.+
  N12: M1.pin12, VCC1.-
  N13: S1.Pin_1, S1.Pin_2
  N14: S1.Pin_3, S1.Pin_4

custom parts:
  BTS7960: BTS7960 43A Peak Power H-Bridge PWM Motor Driver
